# Fritzing sketch sketch_fritzing (saved by Fritzing 0.9.5d)
breadboards: 1

parts:
  U1 = ESP32-38PinWide [part_number=ESP32-38PinWide]
  Sensor_2 = HC-SR04 Ultrasonic Distance Sensor
  Sensor_1 = HC-SR04 Ultrasonic Distance Sensor
  M1 = ac light dimmer-4terminal
  R1 = Photocell (LDR) [package=THT]
  220R = Resistor [tolerance=±5% resistance=220 package="2010 [SMD]"]
  LED = LEDs [package=led10mm]
  V1 = AC Power [voltage=5 frequency=60]
  Part3 = Lilypad Battery Connect  # not connected
  AC_220V = LilyPad Slide Switch  # not connected

nets (from the schematic view):
  N1: U1.GPIO35, R1.pin_0, 220R.Pin_1
  N2: U1.GPIO12, Sensor_1.GND
  N3: U1.GPIO13, Sensor_1.TRIG
  VCC: U1.VIN, Sensor_2.VCC, Sensor_1.VCC, M1.VCC, R1.pin_1
  N4: U1.GPIO16, Sensor_2.GND
  N5: U1.GPIO17, Sensor_2.TRIG
  N6: U1.GPIO5, M1.Z-C
  N7: U1.GPIO23, M1.PWM
  N8: Sensor_2.ECHO, M1.GND
  N9: Sensor_1.ECHO, 220R.Pin_0
  N10: M1.LOAD2, LED.A
  N11: M1.AC-IN1, V1.V+
  N12: M1.AC-IN2, V1.V-

custom parts:
  ESP32-38PinWide: Generic 38-Pin ESP32 with wide format (only access to one side of pins on a breadboard) based on Stephen Lilley's HiLetgo ESP-WROOM-32 ESP32 ESP-32S Development Board.
  ac light dimmer-4terminal: ac light dimmer module 4terminal.
  LEDs: LEDs Standard schematic elements and footprints for 5mm, 3mm, 1206, and 0603 sized LEDs. 5mm - Spark Fun Electronics SKU : COM-00529 (and others)
